# Fritzing sketch digitalwk11 (saved by Fritzing 0.9.3b)
breadboards: 1

parts:
  元件1 = Arduino Uno (Rev3)
  LED1 = LED - 5mm [color="Red (633nm)" package="5 mm [THT]"]
  R1 = Resistor [tolerance=±5% resistance=220 package=THT]
  LED2 = LED - 5mm [color="Red (633nm)" package="5 mm [THT]"]

nets:
  N1: 元件1.GND, LED2.cathode
  N2: 元件1.5V, R1.Pin_0
  N3: LED1.anode, R1.Pin_1, LED2.anode
